# Fritzing sketch datalogger (saved by Fritzing 0.9.3b)
circuit board: 8.28085cm x 5.65252cm
breadboards: 1

parts:
  C1 = Tantalum Capacitor [capacitance=100nF package="B 3528 [SMD, tantalum]"]
  C3 = Tantalum Capacitor [capacitance=100nF package="B 3528 [SMD, tantalum]"]
  C2 = Tantalum Capacitor [capacitance=0.1nF package="B 3528 [SMD, tantalum]"]
  Power_plug1 = Power plug
  U1 = Voltage Regulator [package=v-reg_dpack]
  U2 = SD_CARD_SOCKET [package=sdcard_4uconn]
  U3 = ATmega328 [package=tqfp]
  RESET = Pushbutton [package="[THT]"]
  R1 = Resistor [tolerance=±5% resistance=1M package="1206 [SMD]"]
  L1 = Inductor [inductance=10nH package="1206 [SMD]"]
  C4 = Ceramic Capacitor [capacitance=100nF package="1206 [SMD, multilayer]"]
  Q1 = Basic FET P-Channel [package="DPak [SMD]"]
  FTDI_Friend = male pin header, 6 pins [form="♂ (male)"]
  C5 = Ceramic Capacitor [capacitance=100nF package="1206 [SMD, multilayer]"]
  BAT1 = Battery Holders [package=battcon_20mm]
  WAKE_UP = Pushbutton [package="[THT]"]
  R2 = Resistor [tolerance=±5% resistance=10k package="1206 [SMD]"]
  R3 = Resistor [tolerance=±5% resistance=10k package="1206 [SMD]"]
  C6 = Electrolytic Capacitor [capacitance=1µF package="0405 [SMD, electrolytic]"]
  OneWire = Molex Picoblade Series Header [part_number=0532610319 package=Picoblade-53261-0319]
  R4 = Resistor [tolerance=±5% resistance=4.7k package="1206 [SMD]"]
  RTC = SO16w [chip_label=DS3231SN package=SO(w)]

nets:
  GND: C1.-, C3.-, C2.-, Power_plug1.GND, U1.ADJ, U2.SH, U2.VSS1, U2.VSS2, U3.GND, RESET.Pin_3, RESET.Pin_4, C4.0, FTDI_Friend.pin1, FTDI_Friend.pin2, BAT1.-, WAKE_UP.Pin_1, WAKE_UP.Pin_2, C6.-, OneWire.3, RTC.5, RTC.6, RTC.7, RTC.8, RTC.9, RTC.10, RTC.11, RTC.12, RTC.13
  6V: C1.+, Power_plug1.VCC, U1.IN, FTDI_Friend.pin3
  3.3V: C3.+, C2.+, U1.OUT, U2.VDD, U3.VCC, U3.AREF, R1.Pin_0, L1.pin_0, Q1.source, R2.Pin_0, R3.Pin_0, RTC.2
  CS: U2.CD_DAT3, U3.PB2(SS_OC1B)
  MOSI: U2.CMD, U3.PB3(MOSI_OC2)
  SCK: U2.CLK, U3.PB5(SCK)
  MISO: U2.DAT0, U3.PB4(MISO)
  N1: U3.PD5(T1), Q1.Gate
  DATA: U3.PB0(ICP), OneWire.2, R4.Pin_1
  AVCC: U3.AVCC, L1.pin_1, C4.1
  INT/SQW: U3.PC2(ADC2), WAKE_UP.Pin_3, WAKE_UP.Pin_4, RTC.3
  SDA: U3.PC4(ADC4_SDA), R3.Pin_1, RTC.15
  SCL: U3.PC5(ADC5_SCL), R2.Pin_1, RTC.16
  RESET: U3.PC6(_RESET), RESET.Pin_1, RESET.Pin_2, R1.Pin_1, C5.1
  N2: U3.PD0(RXD), FTDI_Friend.pin4
  N3: U3.PD1(TXD), FTDI_Friend.pin5
  VSS Switched: Q1.drain, OneWire.1, R4.Pin_0
  N4: FTDI_Friend.pin6, C5.0
  N5: BAT1.+, C6.+, RTC.14
  32kHz: RTC.1

notes:
  UW Datalogger, A datalogger for long term deployment. , 2
